// Logisim project EX_MEM_buffer.circ as structural Verilog: 1 circuit, main circuit EX_MEM
module EX_MEM (
  input  clk,
  input  [31:0] Result,
  input  [31:0] RD2,
  input  [4:0] Write,
  input  Zero,
  output [31:0] n_Result,
  output [31:0] n_RD2,
  output [4:0] n_Write,
  output n_Zero
);

  Register #(.width(32)) register_1 (.D(Result), .en(1'b1), .clk(clk), .Q(n_Result));  // open: clr
  Register #(.width(32)) register_2 (.D(RD2), .en(1'b1), .clk(clk), .Q(n_RD2));  // open: clr
  Register #(.width(1)) register_3 (.D(Zero), .en(1'b1), .clk(clk), .Q(n_Zero));  // open: clr
  Register #(.width(5)) register_4 (.D(Write), .en(1'b1), .clk(clk), .Q(n_Write));  // open: clr

  // Notes on the sheet:
  //   inputs
  //   outputs
endmodule
