// Logisim project ID_EX_buffer.circ as structural Verilog: 1 circuit, main circuit ID_EX
module ID_EX (
  input  clk,
  input  [31:0] PC,
  input  [31:0] RD1,
  input  [31:0] RD2,
  input  [31:0] Ext,
  input  [4:0] instr1,
  input  [4:0] instr2,
  output [31:0] n_PC,
  output [31:0] n_RD1,
  output [31:0] n_RD2,
  output [31:0] n_Ext,
  output [4:0] n_instr1,
  output [4:0] n_instr2
);

  Register #(.width(32)) register_1 (.D(PC), .en(1'b1), .clk(clk), .Q(n_PC));  // open: clr
  Register #(.width(32)) register_2 (.D(RD1), .en(1'b1), .clk(clk), .Q(n_RD1));  // open: clr
  Register #(.width(32)) register_3 (.D(RD2), .en(1'b1), .clk(clk), .Q(n_RD2));  // open: clr
  Register #(.width(32)) register_4 (.D(Ext), .en(1'b1), .clk(clk), .Q(n_Ext));  // open: clr
  Register #(.width(5)) register_5 (.D(instr1), .en(1'b1), .clk(clk), .Q(n_instr1));  // open: clr
  Register #(.width(5)) register_6 (.D(instr2), .en(1'b1), .clk(clk), .Q(n_instr2));  // open: clr

  // Notes on the sheet:
  //   inputs
  //   outputs
endmodule
