// Logisim project MemAddressGen.circ as structural Verilog: 1 circuit, main circuit MemAddressGen
module MemAddressGen (
  input  [13:0] address,
  input  miss,
  input  clk,
  input  read,
  output [3:0] memmask,
  output [13:0] memaddress,
  output readmem
);

  wire not_1_out;

  not not_1 (not_1_out, read);
  or or_1 (memmask[3], read, not_1_out);

  assign memmask[2:0] = {3{memmask[3]}};
  assign readmem = read;

  // Other names for the same wires on the sheet: address_t[13:2] = address[13:2]

  // Notes on the sheet:
  //   Inputs
  //   output
endmodule
