// Logisim project cpu.circ as structural Verilog: 1 circuit, main circuit cpu
module cpu (
  input  in_1,
  input  [3:0] in_2,
  input  [31:0] in_3
);

  wire ALUOpValid, ALUSrc, and_1_out, and_2_out, Branch, clk, is_op, JAL, Jump, JumpReg, LB, MemToReg,
       not_1_out, not_2_out, not_3_out, not_4_out, not_5_out, not_6_out, RegDes, RegWrite, SLTi, syscall,
       zero;
  wire [3:0] MemMask;
  wire [4:0] instr2, instr3, multiplexer_2_out, multiplexer_3_out;
  wire [5:0] ALUOp, func, opcd_fnc, opcode;
  wire [15:6] instr0;
  wire [31:0] adder_1_out, adder_2_out, extended, final_writeData, MemData, memWriteData, multiplexer_4_out,
       multiplexer_5_out, multiplexer_7_out, new_PC, PC, rdData2, RegisterFile_p7, result, shifter_1_out,
       writeData;

  not not_1 (not_1_out, syscall);
  Register #(.width(32)) register_1 (.D(new_PC), .en(not_1_out), .clk(clk), .Q(PC), .clr(in_1));
  Adder #(.width(32)) adder_1 (.a(PC), .b(32'h4), .out(adder_1_out), .cin(1'b0));  // open: cout
  not not_2 (not_2_out, clk);
  Clock clock_1 (.out(clk));
  // mem InstMem: pin names not known; wires that end beside it: PC, in_2, in_3, not_2_out, {opcode, instr3, instr2, instr0, func}
  Multiplexer #(.width(32)) multiplexer_1 (
    .in0(writeData), .in1({rdData2[31:8], writeData[7:0]}), .out(final_writeData), .sel(LB));
  Shifter #(.width(32)) shifter_1 (.in(extended), .\dist (5'b00010), .out(shifter_1_out));
  Multiplexer #(.width(5)) multiplexer_2 (.in0(instr2), .in1(instr0[15:11]), .out(multiplexer_2_out), .sel(RegDes));
  Adder #(.width(32)) adder_2 (.a(adder_1_out), .b(shifter_1_out), .out(adder_2_out), .cin(1'b0));  // open: cout
  Multiplexer #(.width(5)) multiplexer_3 (.in0(multiplexer_2_out), .in1({5{1'b1}}), .out(multiplexer_3_out), .sel(JAL));
  Multiplexer #(.width(32)) multiplexer_4 (.in0(final_writeData), .in1(PC), .out(multiplexer_4_out), .sel(JAL));
  Multiplexer #(.width(32)) multiplexer_5 (
    .in0(adder_1_out), .in1(adder_2_out), .out(multiplexer_5_out), .sel(and_1_out));
  and and_1 (and_1_out, zero, Branch);
  Multiplexer #(.width(32)) multiplexer_6 (
    .in0(multiplexer_5_out), .in1({PC[31:28], instr3, instr2, instr0, func, 2'b00}), .out(new_PC), .sel(Jump));
  SignExtend signextend_1 (.inpt({instr0, func}), .opcode(opcode), .outpt(extended));
  // regfile RegisterFile: pin names not known; wires that end beside it: instr3, instr2, multiplexer_4_out, RegWrite, clk, multiplexer_3_out, RegisterFile_p7, rdData2
  Multiplexer #(.width(32)) multiplexer_7 (.in0(rdData2), .in1(extended), .out(multiplexer_7_out), .sel(ALUSrc));
  ControlUnit controlunit_1 (
    .Opcode(opcode), .Func(func), .ALUSrc(ALUSrc), .RegWrite(RegWrite), .ALUOp(ALUOp),
    .ALUOpValid(ALUOpValid), .MemMask(MemMask), .JAL(JAL), .JumpReg(JumpReg), .RegDest(RegDes), .Jump(Jump),
    .Branch(Branch), .LB(LB), .MemToReg(MemToReg), .Syscall(syscall), .SLTi(SLTi));
  aluControl alucontrol_1 (.func(func), .aluOP(ALUOp), .opcd_fnc(opcd_fnc), .is_op(is_op));
  alu alu_1 (
    .rs(RegisterFile_p7), .rt_imm(multiplexer_7_out), .opcd_fnc(opcd_fnc), .shft_amt(instr0[10:6]),
    .is_i(is_op), .result(result), .zero(zero));
  not not_3 (not_3_out, clk);
  // mem DataMem: pin names not known; wires that end beside it: result, MemMask, memWriteData, not_3_out, MemData
  Multiplexer #(.width(32)) multiplexer_8 (.in0(result), .in1(MemData), .out(writeData), .sel(MemToReg));
  not not_4 (not_4_out, MemMask[0]);
  not not_5 (not_5_out, MemMask[1]);
  not not_6 (not_6_out, MemMask[2]);
  and and_2 (and_2_out, not_4_out, not_5_out, not_6_out, MemMask[3]);
  Multiplexer #(.width(32)) multiplexer_9 (
    .in0(rdData2), .in1({MemData[31:8], rdData2[7:0]}), .out(memWriteData), .sel(and_2_out));

  // Other names for the same wires on the sheet: instr0[5:0] = func; Jinstr[25:0] = {instr3, instr2, instr0, func};
  //   sh_amount[4:0] = instr0[10:6]; instr1[4:0] = instr0[15:11]
endmodule
